# Fritzing sketch arai (saved by Fritzing 0.3.10b)
breadboards: 1

parts:
  Arduino1 = Arduino
  R1 = Resistor [resistance=220 package=THT]
  R1_2 = Resistor [resistance=220 package=THT]
  R1_3 = Resistor [resistance=220 package=THT]
  R2 = Photocell (LDR) [package=THT]
  R3 = Temperature Sensor (Thermistor) [package=THT]

nets:
  N1: Arduino1.GND, R1.Pin_1, R1_2.Pin_1, R1_3.Pin_1
  N2: Arduino1.3V3, R1_2.Pin_0, R3.pin_1
  N3: Arduino1.+5V, R2.pin_0, R3.pin_0
  N4: R1_3.Pin_0, R2.pin_1
